# Fritzing sketch Pool-Controller (saved by Fritzing 0.9.3b)
breadboards: 2

parts:
  U1 = 16-Channel Relay Module [package=relay-16ch]
  Raspberry_Pi_1 = Raspberry Pi 3 [part_number=RPI-3-V1.2]
  R1 = Resistor [tolerance=±5% resistance=1k package=THT]
  R2 = Resistor [tolerance=±5% resistance=1k package=THT]
  R3 = Resistor [tolerance=±5% resistance=1k package=THT]
  R4 = Resistor [tolerance=±5% resistance=1k package=THT]
  R5 = Resistor [tolerance=±5% resistance=1k package=THT]
  R6 = Resistor [tolerance=±5% resistance=1k package=THT]
  R7 = Resistor [tolerance=±5% resistance=1k package=THT]
  R8 = Resistor [tolerance=±5% resistance=1k package=THT]
  R9 = Resistor [tolerance=±5% resistance=1k package=THT]
  J1 = Camdenboss CTB0158-6 [part_number=CTB0158-6 package=THT]
  DS1 = DS18B20 1-Wire Temperature Sensor [part_number=DS18B20]
  DS2 = DS18B20 1-Wire Temperature Sensor [part_number=DS18B20]
  J3 = Camdenboss CTB0158-2 [part_number=CTB0158-2 package=THT]
  J4 = Camdenboss CTB0158-2 [part_number=CTB0158-2 package=THT]
  J5 = Camdenboss CTB0158-2 [part_number=CTB0158-2 package=THT]
  J6 = Camdenboss CTB0158-2 [part_number=CTB0158-2 package=THT]
  J7 = Camdenboss CTB0158-4 [part_number=CTB0158-4 package=THT]
  R10 = Resistor [tolerance=±5% resistance=10k package=THT]

nets (from the breadboard view):
  N1: U1.VCC, J1.terminal_1
  N2: U1.GND, J1.terminal_2
  N3: U1.IN1, R1.Pin_0
  N4: U1.IN2, R2.Pin_0
  N5: U1.IN3, R3.Pin_0
  N6: U1.IN4, R4.Pin_0
  N7: U1.IN5, R5.Pin_0
  N8: U1.IN6, R6.Pin_0
  N9: U1.IN7, R7.Pin_0
  N10: U1.IN8, R8.Pin_0
  N11: U1.IN9, R9.Pin_0
  N12: U1.VCCOUT_5V, Raspberry_Pi_1.5V
  N13: U1.K1_COM, J6.terminal_2
  N14: U1.K1_NC, U1.K2_NC, U1.K3_NC, U1.K4_NC, J1.terminal_3, J7.pin4
  N15: U1.K2_COM, J5.terminal_2
  N16: U1.K3_COM, J4.terminal_2
  N17: U1.K4_COM, J3.terminal_2
  3V3: Raspberry_Pi_1.3v3, Raspberry_Pi_1.3V3, R10.Pin_1
  N18: Raspberry_Pi_1.GPIO4, DS1.DQ, DS2.DQ, R10.Pin_0
  N19: Raspberry_Pi_1.GPIO5, R6.Pin_1
  N20: Raspberry_Pi_1.GPIO6, R5.Pin_1
  N21: Raspberry_Pi_1.GPIO13, R9.Pin_1
  N22: Raspberry_Pi_1.GPIO19, R8.Pin_1
  N23: Raspberry_Pi_1.GPIO26, R7.Pin_1
  N24: Raspberry_Pi_1.GPIO21, R1.Pin_1
  N25: Raspberry_Pi_1.GPIO20, R2.Pin_1
  N26: Raspberry_Pi_1.GPIO16, R3.Pin_1
  N27: Raspberry_Pi_1.GPIO12, R4.Pin_1
  GND: Raspberry_Pi_1.GND, DS1.GND, DS2.GND
  N28: J1.pin4, J5.terminal_1, J6.terminal_1, J7.pin1
  N29: J1.terminal_4, J3.terminal_1, J4.terminal_1
  VDD: DS1.VDD, DS2.VDD

notes:
  24 VDC
  24 VAC
  12 VDC
  GPIO 12
  Pump 4
  GPIO 16
  Pump 3
  GPIO 20
  Pump 2
  GPIO 21
  Pump 1
  GPIO 6
  Heater Spa
  GPIO 5
  Heater Pump
  GPIO 26
  Valve Return
  GPIO 19
  Valve Suction
  GPIO 13
  Blower
  IntelliComm® II Interface Adapter
  PUMP
  MASTTEMP External Control Interface
  DS18B20
  Ambient
  DS18B20
  Pool

custom parts:
  16-Channel Relay Module: 16 channel relay module
